# Fritzing sketch PCB_compactadora (saved by Fritzing 0.9.3b)
circuit board: 15cm x 11cm
breadboards: 1

parts:
  V1A = DC Power [voltage=5V]
  RelevadorRLED = IC, DIP package, 6 pins [chip_label=IC]
  RelevadorGLED = IC, DIP package, 6 pins [chip_label=IC]
  RelevadorL = IC, DIP package, 6 pins [chip_label=IC]
  RelevadorR = IC, DIP package, 6 pins [chip_label=IC]
  V4 = DC Power [voltage=24V]
  V3 = DC Power [voltage=12V]
  V2 = DC Power [voltage=12V]
  V3_2 = DC Power [voltage=24V]
  Arduino_MEGA = Arduino Mega 2560 (Rev3)
  Load_cell = Camdenboss CTB0158-5 [part_number=CTB0158-5 package=THT]
  Load_Amp_1 = IC, SIP package, 5 pins [chip_label=HX711]
  Load_Amp_2 = IC, SIP package, 5 pins [chip_label=IC]
  Electroválvula = Camdenboss CTB0158-3 [package=THT]
  Red_Led = Camdenboss CTB0158-2 [part_number=CTB0158-2 package=THT]
  Green_Led = Camdenboss CTB0158-2 [part_number=CTB0158-2 package=THT]
  Door_Switch = Camdenboss CTB0158-2 [part_number=CTB0158-2 package=THT]
  Speaker = Camdenboss CTB0158-2 [part_number=CTB0158-2 package=THT]
  ON_Switch = Camdenboss CTB0158-2 [part_number=CTB0158-2 package=THT]
  Emergency_button = Camdenboss CTB0158-2 [part_number=CTB0158-2 package=THT]
  Compact_button = Camdenboss CTB0158-2 [part_number=CTB0158-2 package=THT]
  Lift_button = Camdenboss CTB0158-2 [part_number=CTB0158-2 package=THT]
  Touch_Screen = Camdenboss CTB0158-4 [part_number=CTB0158-4 package=THT]

nets:
  N1: V1A.V+, Touch_Screen.pin4
  GND: V1A.V-, RelevadorRLED.pin2, RelevadorGLED.pin2, RelevadorL.pin2, RelevadorL.pin5, RelevadorR.pin2, RelevadorR.pin5, V3.V-, V2.V-, Arduino_MEGA.GND, Load_Amp_1.pin5, Electroválvula.pin3, Red_Led.pin2, Green_Led.pin2, Door_Switch.pin2, Speaker.pin2, ON_Switch.pin2, Emergency_button.pin2, Compact_button.pin2, Lift_button.pin2, Touch_Screen.pin1
  N2: RelevadorRLED.pin1, RelevadorGLED.pin1, RelevadorL.pin1, RelevadorR.pin1, Arduino_MEGA.5V, Load_Amp_1.pin1, Load_Amp_1.pin2
  N3: RelevadorRLED.pin3, Arduino_MEGA.D46
  N4: RelevadorRLED.pin4, Red_Led.pin1
  N5: RelevadorRLED.pin5, V2.V+
  N6: RelevadorGLED.pin3, Arduino_MEGA.D42
  N7: RelevadorGLED.pin4, Green_Led.pin1
  N8: RelevadorGLED.pin5, V3.V+
  N9: RelevadorL.pin3, Arduino_MEGA.D28
  N10: RelevadorL.pin4, V3_2.V-
  N11: RelevadorR.pin3, Arduino_MEGA.D29
  N12: RelevadorR.pin4, V4.V-
  N13: V4.V+, Electroválvula.pin2
  N14: V3_2.V+, Electroválvula.pin1
  N15: Arduino_MEGA.D9_PWM, Speaker.pin1
  N16: Arduino_MEGA.D0_RX0, Touch_Screen.pin3
  N17: Arduino_MEGA.D1_TX0, Touch_Screen.pin2
  N18: Arduino_MEGA.D3_PWM, ON_Switch.pin1
  N19: Arduino_MEGA.D4_PWM, Load_Amp_1.pin3
  N20: Arduino_MEGA.D5_PWM, Load_Amp_1.pin4
  N21: Arduino_MEGA.D23, Door_Switch.pin1
  N22: Arduino_MEGA.D33, Lift_button.pin1
  N23: Arduino_MEGA.D35, Emergency_button.pin1
  N24: Arduino_MEGA.D37, Compact_button.pin1
  N25: Load_cell.pin1, Load_Amp_2.pin1
  N26: Load_cell.pin2, Load_Amp_2.pin2
  N27: Load_cell.pin3, Load_Amp_2.pin3
  N28: Load_cell.pin4, Load_Amp_2.pin4
  N29: Load_cell.pin5, Load_Amp_2.pin5
